# Fritzing sketch MVP (saved by Fritzing 0.9.4)

parts:
  Part1 = Adafruit Si7021 Temp Humidity [part_number=Si7021]
  4_Channel_Relay1 = 4 Channel Power Relay
  EXHAUST_FAN = Fan - Ventilador [package=THT]
  Power_plug1 = Power plug
  12_V_ADAPTER = Transformer [package=transformer]
  LED_LIGHTS = LEDs [package=led10mm]
  Raspberry_Pi_3_B+ = Raspberry Pi 3 [part_number=RPI-3B+]

nets:
  N1: Part1.SDA, Raspberry_Pi_3_B+.GPIO2
  N2: Part1.SCL, Raspberry_Pi_3_B+.GPIO3
  GND: Part1.GND, 4_Channel_Relay1.GND, Raspberry_Pi_3_B+.GND
  +3V3: Part1.+3V3, Raspberry_Pi_3_B+.3v3
  N3: 4_Channel_Relay1.IN1, Raspberry_Pi_3_B+.GPIO19
  N4: 4_Channel_Relay1.IN2, Raspberry_Pi_3_B+.GPIO6
  N5: 4_Channel_Relay1.IN3, Raspberry_Pi_3_B+.GPIO13
  N6: 4_Channel_Relay1.IN4, Raspberry_Pi_3_B+.GPIO5
  VCC: 4_Channel_Relay1.VCC, Raspberry_Pi_3_B+.5V
  N7: 4_Channel_Relay1.NC, EXHAUST_FAN.5V
  N8: 4_Channel_Relay1.COM#17, 12_V_ADAPTER.1
  N9: 4_Channel_Relay1.COM#26, Power_plug1.GND
  N10: 4_Channel_Relay1.NO, LED_LIGHTS.A
  N11: EXHAUST_FAN.GND, 12_V_ADAPTER.4
  N12: Power_plug1.VCC, LED_LIGHTS.C

custom parts:
  Adafruit Si7021 Temp Humidity: It's summer and you're sweating and your hair's all frizzy and all you really want to know is why the weatherman said this morning that today's relative humidity would max out at a perfectly reasonable 42% when it feels more like 77%. Enter the Si7021 Temperature + Humidity Sensor - the best way to prove the weatherman wrong! This lovely sensor for Silicon labs has ± 3% relative humidity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
  4 Channel Power Relay: A 4 channel power relay. The module operates at 5V.
  Fan - Ventilador: Ventilador de 2 pines, se encuentra comunmente en computadoras de escritorio
